# Fritzing sketch Pi MotorBike V2 (saved by Fritzing 0.9.3b)

parts:
  BRD1 = KidBright32 [package=breakout]
  MD1 = Maker Drive
  KY-1 = Keyes Relay [package=THT]
  BAT1 = 12 battery [package=battery]
  S3 = Toggle Switch spdt [package=THT]
  R1 = Resistor [tolerance=±5% resistance=220 package=THT]
  BUTTON1 = Arcade Button (red)
  U1 = SWITCH-SPST-2 [package=switch-spst-vertical]  # not connected
  S4 = Limit Switch [package="Breakout Board"]
  M1 = DC Motor
  M2 = DC Motor  # not connected
  M3 = RioRand LM2596
  Part1 = NeoPixel Stick [part_number=1426]
  Part2 = NeoPixel Stick [part_number=1426]
  D1 = Schottky Diode [part_number=1N5817 package="Melf DO-213 AB [SMD]"]
  R3 = Resistor [tolerance=±5% resistance=220 package=THT]
  R4 = Resistor [tolerance=±5% resistance=220 package=THT]
  R5 = Resistor [tolerance=±5% resistance=220 package=THT]
  R6 = Resistor [tolerance=±5% resistance=220 package=THT]

nets:
  N1: BRD1.J1_1, KY-1.signal
  N2: BRD1.J1_5, KY-1.power
  N3: BRD1.J1_7, Part1.DATAIN
  N4: BRD1.J5_1, R1.Pin_0, R6.Pin_0
  N5: BRD1.J5_2, M3.Pin_3, D1.anode, R3.Pin_0, R4.Pin_0, R5.Pin_0
  N6: BRD1.J5_3, S3.L2, R3.Pin_1
  N7: BRD1.J5_4, S3.L1, R4.Pin_1
  N8: BRD1.J5_5, S4.V, R5.Pin_1
  N9: BRD1.J5_7, MD1.M1A_IO, R1.Pin_1
  N10: BRD1.J5_8, MD1.M1B_IO, R6.Pin_1
  N11: BRD1.J5_9, MD1.GND, S3.COM, S4.S
  N12: BRD1.J5_10, KY-1.ground, M3.Pin_4
  N13: MD1.VB+, KY-1.C, M3.Pin_1
  N14: MD1.VB-, BAT1.-, BUTTON1.no_name_yet#2, M3.Pin_2
  N15: MD1.M1A, M1.pin_2
  N16: MD1.M1B, M1.pin_1
  N17: KY-1.NO, BUTTON1.no_name_yet#1
  N18: Part1.DATAOUT, Part2.DATAIN
  +5V: Part1.+5V, Part2.+5V
  GND: Part1.GND, Part2.GND, D1.cathode

notes:
  R10k
  Foot SW
  FW/RW SW
  Power SW
  12 to 5V
  Motor Control
  Relay Module
  Siren
  8LED(L) Neopixel
  8LED(R) Neopixel
  Motor
  Diode
  1N4007

custom parts:
  KidBright32: KidBright32 Board
  Maker Drive: Simplifying H-Bridge Motor Driver for Beginner.
  Keyes Relay: The Keyes 5V relay module is suitable for SCM development, home appliance control. It uses a 5V~12V TIL control signal which can control DC / AC signal.
  12 battery: 12V lead acid type battery, like the Husqvarna YTH2448 12V 35AH battery. This is the mini version 1/4 the size of the actual battery to be closer to typical breadboard parts (around 2in wide rathher than 7in). The pads in pcb are sized to accomidate up to 14ga wire (as these batterys will deliver high currents.)
  Toggle Switch spdt: Toggle Switch single pole double throw
  Arcade Button (red): Adafruit Arcade Button (red)
  Limit Switch: Generic limit switch commonly found on 3D printers. Typical lever microswitch mounted on a PCB board with a 3 pin JST XH connector.
  NeoPixel Stick: Make your own little LED strip arrangement with this stick of NeoPixel LEDs. We crammed 8 of the tiny 5050 (5mm x 5mm) smart RGB LEDs onto a PCB with mounting holes and a chainable design. Use only one microcontroller pin to control as many as you can chain together! Each LED is addressable as the driver chip is inside the LED. Each one has ~18mA constant current drive so the color will be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
